# Fritzing sketch Diagrama_Alarma (saved by Fritzing 0.9.3b)
breadboards: 1

parts:
  J1 = Piezo Speaker
  S1 = SWITCH-MOMENTARY-2 [package=reed_switch_plastic]
  LED1 = smd LED [color="Blue (525nm)" package="1206 [SMD]"]
  R1 = Resistor [tolerance=±5% resistance=10 package="1206 [SMD]"]
  R2 = Resistor [tolerance=±5% resistance=220 package="1206 [SMD]"]
  R3 = Resistor [tolerance=±5% resistance=100 package="1206 [SMD]"]
  Componente1 = Arduino Uno (Rev3) - ICSP

nets:
  N1: J1.pin1, LED1.cathode, R1.Pin_0, Componente1.GND
  N2: J1.pin2, R3.Pin_1
  N3: S1.1, R1.Pin_1, Componente1.D2
  N4: S1.2, Componente1.5V
  N5: LED1.anode, R2.Pin_1
  N6: R2.Pin_0, Componente1.ICSP_MISO, Componente1.D12/MISO
  N7: R3.Pin_0, Componente1.D8
